# Fritzing sketch schematic_R2R (saved by Fritzing 0.9.3b)
breadboards: 1

parts:
  S33 = SWITCH-MOMENTARY-2 [package=tactile_switch_smd]
  S34 = SWITCH-MOMENTARY-2 [package=tactile_switch_smd]
  S35 = SWITCH-MOMENTARY-2 [package=tactile_switch_smd]
  S36 = SWITCH-MOMENTARY-2 [package=tactile_switch_smd]
  S37 = SWITCH-MOMENTARY-2 [package=tactile_switch_smd]
  S38 = SWITCH-MOMENTARY-2 [package=tactile_switch_smd]
  S39 = SWITCH-MOMENTARY-2 [package=tactile_switch_smd]
  S40 = SWITCH-MOMENTARY-2 [package=tactile_switch_smd]
  2R = Resistor [tolerance=±5% resistance=22k package=THT]
  2R_2 = Resistor [tolerance=±5% resistance=22k package=THT]
  R = Resistor [tolerance=±5% resistance=10k package=THT]
  2R_3 = Resistor [tolerance=±5% resistance=22k package=THT]
  R_2 = Resistor [tolerance=±5% resistance=10k package=THT]
  R_3 = Resistor [tolerance=±5% resistance=10k package=THT]
  2R_4 = Resistor [tolerance=±5% resistance=22k package=THT]
  R_4 = Resistor [tolerance=±5% resistance=10k package=THT]
  R_5 = Resistor [tolerance=±5% resistance=10k package=THT]
  R_6 = Resistor [tolerance=±5% resistance=10k package=THT]
  2R_5 = Resistor [tolerance=±5% resistance=22k package=THT]
  2R_6 = Resistor [tolerance=±5% resistance=22k package=THT]
  2R_7 = Resistor [tolerance=±5% resistance=22k package=THT]
  R_7 = Resistor [tolerance=±5% resistance=10k package=THT]
  2R_8 = Resistor [tolerance=±5% resistance=22k package=THT]
  2R_9 = Resistor [tolerance=±5% resistance=22k package=THT]

nets:
  5V: S33.1, S34.1, S35.1, S36.1, S37.1, S38.1, S39.1, S40.1
  N1: S33.2, 2R_5.Pin_0
  N2: S34.2, 2R.Pin_0
  N3: S35.2, 2R_3.Pin_0
  N4: S36.2, 2R_9.Pin_0
  N5: S37.2, 2R_2.Pin_0
  N6: S38.2, 2R_4.Pin_0
  N7: S39.2, 2R_6.Pin_0
  N8: S40.2, 2R_8.Pin_0
  Output: 2R.Pin_1, R_4.Pin_1
  N9: 2R_2.Pin_1, 2R_7.Pin_1, R_7.Pin_0
  N10: R.Pin_0, R_3.Pin_1, 2R_8.Pin_1
  N11: R.Pin_1, 2R_4.Pin_1, R_6.Pin_0
  N12: 2R_3.Pin_1, R_2.Pin_1, R_5.Pin_0
  N13: R_2.Pin_0, R_6.Pin_1, 2R_5.Pin_1
  N14: R_3.Pin_0, 2R_6.Pin_1, R_7.Pin_1
  N15: R_4.Pin_0, R_5.Pin_1, 2R_9.Pin_1
  GND: 2R_7.Pin_0
