# Fritzing sketch schematic (saved by Fritzing 0.9.3b)

parts:
  DAC01 = IC, DIP package, 16 pins [chip_label=DAC0808]
  MUX01 = IC, DIP package, 16 pins [chip_label=CD4051]
  Part1 = Arduino Uno (Rev3)
  DAC02 = IC, DIP package, 16 pins [chip_label=DAC0808]
  DAC03 = IC, DIP package, 16 pins [chip_label=DAC0808]
  DAC04 = IC, DIP package, 16 pins [chip_label=DAC0808]
  DAC08 = IC, DIP package, 16 pins [chip_label=DAC0808]
  DAC07 = IC, DIP package, 16 pins [chip_label=DAC0808]
  DAC06 = IC, DIP package, 16 pins [chip_label=DAC0808]
  DAC05 = IC, DIP package, 16 pins [chip_label=DAC0808]
  S1 = SWITCH-MOMENTARY-2 [package=tactile_switch_smd]
  LED1 = LEDs [package=led10mm]
  S2 = SWITCH-MOMENTARY-2 [package=tactile_switch_smd]
  LED2 = LEDs [package=led10mm]
  S3 = SWITCH-MOMENTARY-2 [package=tactile_switch_smd]
  LED3 = LEDs [package=led10mm]
  S4 = SWITCH-MOMENTARY-2 [package=tactile_switch_smd]
  LED4 = LEDs [package=led10mm]
  S5 = SWITCH-MOMENTARY-2 [package=tactile_switch_smd]
  S6 = SWITCH-MOMENTARY-2 [package=tactile_switch_smd]
  S7 = SWITCH-MOMENTARY-2 [package=tactile_switch_smd]
  S8 = SWITCH-MOMENTARY-2 [package=tactile_switch_smd]
  LED5 = LEDs [package=led10mm]
  LED6 = LEDs [package=led10mm]
  LED7 = LEDs [package=led10mm]
  LED8 = LEDs [package=led10mm]
  S9 = SWITCH-MOMENTARY-2 [package=tactile_switch_smd]
  S10 = SWITCH-MOMENTARY-2 [package=tactile_switch_smd]
  S11 = SWITCH-MOMENTARY-2 [package=tactile_switch_smd]
  S12 = SWITCH-MOMENTARY-2 [package=tactile_switch_smd]
  S13 = SWITCH-MOMENTARY-2 [package=tactile_switch_smd]
  S14 = SWITCH-MOMENTARY-2 [package=tactile_switch_smd]
  S15 = SWITCH-MOMENTARY-2 [package=tactile_switch_smd]
  S16 = SWITCH-MOMENTARY-2 [package=tactile_switch_smd]
  LED9 = LEDs [package=led10mm]
  LED10 = LEDs [package=led10mm]
  LED11 = LEDs [package=led10mm]
  LED12 = LEDs [package=led10mm]
  LED13 = LEDs [package=led10mm]
  LED14 = LEDs [package=led10mm]
  LED15 = LEDs [package=led10mm]
  LED16 = LEDs [package=led10mm]
  S17 = SWITCH-MOMENTARY-2 [package=tactile_switch_smd]
  S18 = SWITCH-MOMENTARY-2 [package=tactile_switch_smd]
  S19 = SWITCH-MOMENTARY-2 [package=tactile_switch_smd]
  S20 = SWITCH-MOMENTARY-2 [package=tactile_switch_smd]
  S21 = SWITCH-MOMENTARY-2 [package=tactile_switch_smd]
  S22 = SWITCH-MOMENTARY-2 [package=tactile_switch_smd]
  S23 = SWITCH-MOMENTARY-2 [package=tactile_switch_smd]
  S24 = SWITCH-MOMENTARY-2 [package=tactile_switch_smd]
  LED17 = LEDs [package=led10mm]
  LED18 = LEDs [package=led10mm]
  LED19 = LEDs [package=led10mm]
  LED20 = LEDs [package=led10mm]  # not connected
  LED21 = LEDs [package=led10mm]
  LED22 = LEDs [package=led10mm]  # not connected
  LED23 = LEDs [package=led10mm]
  LED24 = LEDs [package=led10mm]
  S25 = SWITCH-MOMENTARY-2 [package=tactile_switch_smd]
  S26 = SWITCH-MOMENTARY-2 [package=tactile_switch_smd]
  S27 = SWITCH-MOMENTARY-2 [package=tactile_switch_smd]
  S28 = SWITCH-MOMENTARY-2 [package=tactile_switch_smd]
  S29 = SWITCH-MOMENTARY-2 [package=tactile_switch_smd]
  S30 = SWITCH-MOMENTARY-2 [package=tactile_switch_smd]
  S31 = SWITCH-MOMENTARY-2 [package=tactile_switch_smd]
  S32 = SWITCH-MOMENTARY-2 [package=tactile_switch_smd]
  LED25 = LEDs [package=led10mm]  # not connected
  LED26 = LEDs [package=led10mm]  # not connected
  LED27 = LEDs [package=led10mm]  # not connected
  LED28 = LEDs [package=led10mm]  # not connected
  LED29 = LEDs [package=led10mm]  # not connected
  LED30 = LEDs [package=led10mm]  # not connected
  LED31 = LEDs [package=led10mm]  # not connected
  LED32 = LEDs [package=led10mm]  # not connected
  S33 = SWITCH-MOMENTARY-2 [package=tactile_switch_smd]
  S34 = SWITCH-MOMENTARY-2 [package=tactile_switch_smd]
  S35 = SWITCH-MOMENTARY-2 [package=tactile_switch_smd]
  S36 = SWITCH-MOMENTARY-2 [package=tactile_switch_smd]
  S37 = SWITCH-MOMENTARY-2 [package=tactile_switch_smd]
  S38 = SWITCH-MOMENTARY-2 [package=tactile_switch_smd]
  S39 = SWITCH-MOMENTARY-2 [package=tactile_switch_smd]
  S40 = SWITCH-MOMENTARY-2 [package=tactile_switch_smd]
  S41 = SWITCH-MOMENTARY-2 [package=tactile_switch_smd]
  S42 = SWITCH-MOMENTARY-2 [package=tactile_switch_smd]
  S43 = SWITCH-MOMENTARY-2 [package=tactile_switch_smd]
  S44 = SWITCH-MOMENTARY-2 [package=tactile_switch_smd]
  S45 = SWITCH-MOMENTARY-2 [package=tactile_switch_smd]
  S46 = SWITCH-MOMENTARY-2 [package=tactile_switch_smd]
  S47 = SWITCH-MOMENTARY-2 [package=tactile_switch_smd]
  S48 = SWITCH-MOMENTARY-2 [package=tactile_switch_smd]
  S49 = SWITCH-MOMENTARY-2 [package=tactile_switch_smd]
  S50 = SWITCH-MOMENTARY-2 [package=tactile_switch_smd]
  S51 = SWITCH-MOMENTARY-2 [package=tactile_switch_smd]
  S52 = SWITCH-MOMENTARY-2 [package=tactile_switch_smd]
  S53 = SWITCH-MOMENTARY-2 [package=tactile_switch_smd]
  S54 = SWITCH-MOMENTARY-2 [package=tactile_switch_smd]
  S55 = SWITCH-MOMENTARY-2 [package=tactile_switch_smd]
  S56 = SWITCH-MOMENTARY-2 [package=tactile_switch_smd]
  S57 = SWITCH-MOMENTARY-2 [package=tactile_switch_smd]
  S58 = SWITCH-MOMENTARY-2 [package=tactile_switch_smd]
  S59 = SWITCH-MOMENTARY-2 [package=tactile_switch_smd]
  S60 = SWITCH-MOMENTARY-2 [package=tactile_switch_smd]
  S61 = SWITCH-MOMENTARY-2 [package=tactile_switch_smd]
  S62 = SWITCH-MOMENTARY-2 [package=tactile_switch_smd]
  S63 = SWITCH-MOMENTARY-2 [package=tactile_switch_smd]
  S64 = SWITCH-MOMENTARY-2 [package=tactile_switch_smd]
  LED33 = LEDs [package=led10mm]
  LED34 = LEDs [package=led10mm]
  LED35 = LEDs [package=led10mm]
  LED36 = LEDs [package=led10mm]
  LED37 = LEDs [package=led10mm]
  LED38 = LEDs [package=led10mm]
  LED39 = LEDs [package=led10mm]
  LED40 = LEDs [package=led10mm]
  LED41 = LEDs [package=led10mm]
  LED42 = LEDs [package=led10mm]
  LED43 = LEDs [package=led10mm]
  LED44 = LEDs [package=led10mm]
  LED45 = LEDs [package=led10mm]
  LED46 = LEDs [package=led10mm]
  LED47 = LEDs [package=led10mm]
  LED48 = LEDs [package=led10mm]
  LED49 = LEDs [package=led10mm]
  LED50 = LEDs [package=led10mm]
  LED51 = LEDs [package=led10mm]
  LED52 = LEDs [package=led10mm]
  LED53 = LEDs [package=led10mm]
  LED54 = LEDs [package=led10mm]
  LED55 = LEDs [package=led10mm]
  LED56 = LEDs [package=led10mm]
  LED57 = LEDs [package=led10mm]
  LED58 = LEDs [package=led10mm]
  LED59 = LEDs [package=led10mm]
  LED60 = LEDs [package=led10mm]
  LED61 = LEDs [package=led10mm]
  LED62 = LEDs [package=led10mm]
  LED63 = LEDs [package=led10mm]
  LED64 = LEDs [package=led10mm]

nets:
  N1: DAC01.pin2, DAC01.pin3, DAC01.pin15, MUX01.pin6, MUX01.pin7, MUX01.pin8, Part1.GND, DAC02.pin2, DAC02.pin3, DAC02.pin15, DAC03.pin2, DAC03.pin15, DAC04.pin15, DAC08.pin2, DAC08.pin3, DAC08.pin15, DAC07.pin2, DAC07.pin3, DAC07.pin15, DAC06.pin2, DAC06.pin3, DAC06.pin15, DAC05.pin2, DAC05.pin3, DAC05.pin15
  N2: DAC01.pin4, MUX01.pin13
  N3: DAC01.pin5, S7.2
  N4: DAC01.pin6, S8.2
  N5: DAC01.pin7, S6.2
  N6: DAC01.pin8, S5.2
  N7: DAC01.pin9, S4.2
  N8: DAC01.pin10, S3.2
  N9: DAC01.pin11, S2.2
  N10: DAC01.pin12, S1.2
  N11: DAC01.pin13, DAC01.pin14, MUX01.pin16, DAC02.pin13, DAC02.pin14, DAC03.pin13, DAC03.pin14, DAC04.pin13, DAC04.pin14, DAC08.pin13, DAC08.pin14, DAC07.pin13, DAC07.pin14, DAC06.pin13, DAC06.pin14, DAC05.pin13, DAC05.pin14, S1.1, LED1.A, S2.1, LED2.A, S3.1, LED3.A, S4.1, LED4.A, S5.1, S6.1, S7.1, S8.1, LED5.A, LED6.A, LED7.A, LED8.A, S9.1, S10.1, S11.1, S12.1, S13.1, S14.1, S15.1, S16.1, LED9.A, LED10.A, LED11.A, LED12.A, LED13.A, LED14.A, LED15.A, LED16.A
  N12: MUX01.pin1, DAC05.pin4
  N13: MUX01.pin2, DAC07.pin4
  N14: MUX01.pin3, Part1.A0
  N15: MUX01.pin4, DAC06.pin4
  N16: MUX01.pin5, DAC08.pin4
  N17: MUX01.pin9, Part1.D4
  N18: MUX01.pin10, Part1.D3_PWM
  N19: MUX01.pin11, Part1.D2
  N20: MUX01.pin12, DAC04.pin4
  N21: MUX01.pin14, DAC02.pin4
  N22: MUX01.pin15, DAC03.pin4
  N23: DAC02.pin5, S13.2
  N24: DAC02.pin6, S14.2
  N25: DAC02.pin7, S12.2
  N26: DAC02.pin8, S15.2
  N27: DAC02.pin9, S10.2
  N28: DAC02.pin10, S16.2
  N29: DAC02.pin11, S11.2
  N30: DAC02.pin12, S9.2
  N31: DAC03.pin3, DAC04.pin2, DAC04.pin3
  N32: DAC03.pin5, S20.2
  N33: DAC03.pin6, S23.2
  N34: DAC03.pin7, S18.2
  N35: DAC03.pin8, S17.2
  N36: DAC03.pin9, S19.2
  N37: DAC03.pin10, S21.2
  N38: DAC03.pin11, S24.2
  N39: DAC03.pin12, S22.2
  N40: DAC04.pin5, S28.2
  N41: DAC04.pin6, S26.2
  N42: DAC04.pin7, S25.2
  N43: DAC04.pin8, S27.2
  N44: DAC04.pin9, S32.2
  N45: DAC04.pin10, S30.2
  N46: DAC04.pin11, S29.2
  N47: DAC04.pin12, S31.2
  N48: S17.1, S18.1, S19.1, S21.1, S22.1, S24.1, LED17.A, LED18.A, LED19.A, LED21.A, LED23.A, LED24.A
  N49: S33.1, LED33.A
  N50: S34.1, LED38.A
  N51: S35.1, LED53.A
  N52: S36.1, LED64.A
  N53: S37.1, LED40.A
  N54: S38.1, LED46.A
  N55: S39.1, LED63.A
  N56: S40.1, LED42.A
  N57: S41.1, LED59.A
  N58: S42.1, LED37.A
  N59: S43.1, LED50.A
  N60: S44.1, LED61.A
  N61: S45.1, LED44.A
  N62: S46.1, LED43.A
  N63: S47.1, LED45.A
  N64: S48.1, LED36.A
  N65: S49.1, LED58.A
  N66: S50.1, LED57.A
  N67: S51.1, LED60.A
  N68: S52.1, LED35.A
  N69: S53.1, LED62.A
  N70: S54.1, LED48.A
  N71: S55.1, LED54.A
  N72: S56.1, LED55.A
  N73: S57.1, LED56.A
  N74: S58.1, LED41.A
  N75: S59.1, LED39.A
  N76: S60.1, LED52.A
  N77: S61.1, LED47.A
  N78: S62.1, LED49.A
  N79: S63.1, LED51.A
  N80: S64.1, LED34.A

// code stored in the sketch: Untitled2.ino
void setup() {

}

void loop() {
	Serial.println(analogRead(A0));
}
