# Fritzing sketch schematic_v2 (saved by Fritzing 0.9.3b)

parts:
  MUX01 = IC, DIP package, 16 pins [chip_label=CD4051]
  Part1 = Arduino Uno (Rev3)
  S25 = SWITCH-MOMENTARY-2 [package=tactile_switch_smd]
  S26 = SWITCH-MOMENTARY-2 [package=tactile_switch_smd]
  S27 = SWITCH-MOMENTARY-2 [package=tactile_switch_smd]
  S28 = SWITCH-MOMENTARY-2 [package=tactile_switch_smd]
  S29 = SWITCH-MOMENTARY-2 [package=tactile_switch_smd]
  S30 = SWITCH-MOMENTARY-2 [package=tactile_switch_smd]
  S31 = SWITCH-MOMENTARY-2 [package=tactile_switch_smd]
  S32 = SWITCH-MOMENTARY-2 [package=tactile_switch_smd]
  R129 = Resistor [tolerance=±5% resistance=22k package=THT]
  R130 = Resistor [tolerance=±5% resistance=22k package=THT]
  R131 = Resistor [tolerance=±5% resistance=22k package=THT]
  R132 = Resistor [tolerance=±5% resistance=22k package=THT]
  R133 = Resistor [tolerance=±5% resistance=22k package=THT]
  R134 = Resistor [tolerance=±5% resistance=22k package=THT]
  R7 = Resistor [tolerance=±5% resistance=22k package=THT]
  R135 = Resistor [tolerance=±5% resistance=22k package=THT]
  R136 = Resistor [tolerance=±5% resistance=22k package=THT]
  R137 = Resistor [tolerance=±5% resistance=10k package=THT]
  R138 = Resistor [tolerance=±5% resistance=10k package=THT]
  R139 = Resistor [tolerance=±5% resistance=10k package=THT]
  R140 = Resistor [tolerance=±5% resistance=10k package=THT]
  R141 = Resistor [tolerance=±5% resistance=10k package=THT]
  R142 = Resistor [tolerance=±5% resistance=10k package=THT]
  R143 = Resistor [tolerance=±5% resistance=10k package=THT]
  S33 = SWITCH-MOMENTARY-2 [package=tactile_switch_smd]
  S34 = SWITCH-MOMENTARY-2 [package=tactile_switch_smd]
  S35 = SWITCH-MOMENTARY-2 [package=tactile_switch_smd]
  S36 = SWITCH-MOMENTARY-2 [package=tactile_switch_smd]
  S37 = SWITCH-MOMENTARY-2 [package=tactile_switch_smd]
  S38 = SWITCH-MOMENTARY-2 [package=tactile_switch_smd]
  S39 = SWITCH-MOMENTARY-2 [package=tactile_switch_smd]
  S40 = SWITCH-MOMENTARY-2 [package=tactile_switch_smd]
  R2 = Resistor [tolerance=±5% resistance=22k package=THT]
  R2_2 = Resistor [tolerance=±5% resistance=22k package=THT]
  R2_3 = Resistor [tolerance=±5% resistance=22k package=THT]
  R2_4 = Resistor [tolerance=±5% resistance=22k package=THT]
  R144 = Resistor [tolerance=±5% resistance=10k package=THT]
  R2_5 = Resistor [tolerance=±5% resistance=22k package=THT]
  R145 = Resistor [tolerance=±5% resistance=10k package=THT]
  R25 = Resistor [tolerance=±5% resistance=10k package=THT]
  R146 = Resistor [tolerance=±5% resistance=10k package=THT]
  R147 = Resistor [tolerance=±5% resistance=10k package=THT]
  R2_6 = Resistor [tolerance=±5% resistance=22k package=THT]
  R2_7 = Resistor [tolerance=±5% resistance=22k package=THT]
  R148 = Resistor [tolerance=±5% resistance=10k package=THT]
  R149 = Resistor [tolerance=±5% resistance=10k package=THT]
  R2_8 = Resistor [tolerance=±5% resistance=22k package=THT]
  S41 = SWITCH-MOMENTARY-2 [package=tactile_switch_smd]
  S42 = SWITCH-MOMENTARY-2 [package=tactile_switch_smd]
  S43 = SWITCH-MOMENTARY-2 [package=tactile_switch_smd]
  S44 = SWITCH-MOMENTARY-2 [package=tactile_switch_smd]
  S45 = SWITCH-MOMENTARY-2 [package=tactile_switch_smd]
  S46 = SWITCH-MOMENTARY-2 [package=tactile_switch_smd]
  S47 = SWITCH-MOMENTARY-2 [package=tactile_switch_smd]
  S48 = SWITCH-MOMENTARY-2 [package=tactile_switch_smd]
  R33 = Resistor [tolerance=±5% resistance=22k package=THT]
  R34 = Resistor [tolerance=±5% resistance=22k package=THT]
  R35 = Resistor [tolerance=±5% resistance=10k package=THT]
  R36 = Resistor [tolerance=±5% resistance=22k package=THT]
  R37 = Resistor [tolerance=±5% resistance=22k package=THT]
  R38 = Resistor [tolerance=±5% resistance=22k package=THT]
  R39 = Resistor [tolerance=±5% resistance=22k package=THT]
  R40 = Resistor [tolerance=±5% resistance=22k package=THT]
  R41 = Resistor [tolerance=±5% resistance=10k package=THT]
  R42 = Resistor [tolerance=±5% resistance=22k package=THT]
  R43 = Resistor [tolerance=±5% resistance=10k package=THT]
  R44 = Resistor [tolerance=±5% resistance=10k package=THT]
  R45 = Resistor [tolerance=±5% resistance=10k package=THT]
  R46 = Resistor [tolerance=±5% resistance=10k package=THT]
  R47 = Resistor [tolerance=±5% resistance=22k package=THT]
  R48 = Resistor [tolerance=±5% resistance=10k package=THT]
  LED48 = LEDs [package=led10mm]  # not connected
  S49 = SWITCH-MOMENTARY-2 [package=tactile_switch_smd]
  S50 = SWITCH-MOMENTARY-2 [package=tactile_switch_smd]
  S51 = SWITCH-MOMENTARY-2 [package=tactile_switch_smd]
  S52 = SWITCH-MOMENTARY-2 [package=tactile_switch_smd]
  S53 = SWITCH-MOMENTARY-2 [package=tactile_switch_smd]
  S54 = SWITCH-MOMENTARY-2 [package=tactile_switch_smd]
  S55 = SWITCH-MOMENTARY-2 [package=tactile_switch_smd]
  S56 = SWITCH-MOMENTARY-2 [package=tactile_switch_smd]
  R49 = Resistor [tolerance=±5% resistance=22k package=THT]
  R50 = Resistor [tolerance=±5% resistance=10k package=THT]
  R51 = Resistor [tolerance=±5% resistance=22k package=THT]
  R52 = Resistor [tolerance=±5% resistance=22k package=THT]
  R53 = Resistor [tolerance=±5% resistance=22k package=THT]
  R54 = Resistor [tolerance=±5% resistance=10k package=THT]
  R55 = Resistor [tolerance=±5% resistance=10k package=THT]
  R56 = Resistor [tolerance=±5% resistance=10k package=THT]
  R57 = Resistor [tolerance=±5% resistance=22k package=THT]
  R58 = Resistor [tolerance=±5% resistance=10k package=THT]
  R59 = Resistor [tolerance=±5% resistance=10k package=THT]
  R60 = Resistor [tolerance=±5% resistance=10k package=THT]
  R61 = Resistor [tolerance=±5% resistance=22k package=THT]
  R62 = Resistor [tolerance=±5% resistance=22k package=THT]
  R63 = Resistor [tolerance=±5% resistance=22k package=THT]
  R64 = Resistor [tolerance=±5% resistance=22k package=THT]
  S57 = SWITCH-MOMENTARY-2 [package=tactile_switch_smd]
  S58 = SWITCH-MOMENTARY-2 [package=tactile_switch_smd]
  S59 = SWITCH-MOMENTARY-2 [package=tactile_switch_smd]
  S60 = SWITCH-MOMENTARY-2 [package=tactile_switch_smd]
  S61 = SWITCH-MOMENTARY-2 [package=tactile_switch_smd]
  S62 = SWITCH-MOMENTARY-2 [package=tactile_switch_smd]
  S63 = SWITCH-MOMENTARY-2 [package=tactile_switch_smd]
  S64 = SWITCH-MOMENTARY-2 [package=tactile_switch_smd]
  S65 = SWITCH-MOMENTARY-2 [package=tactile_switch_smd]
  S66 = SWITCH-MOMENTARY-2 [package=tactile_switch_smd]
  S67 = SWITCH-MOMENTARY-2 [package=tactile_switch_smd]
  S68 = SWITCH-MOMENTARY-2 [package=tactile_switch_smd]
  S69 = SWITCH-MOMENTARY-2 [package=tactile_switch_smd]
  S70 = SWITCH-MOMENTARY-2 [package=tactile_switch_smd]
  S71 = SWITCH-MOMENTARY-2 [package=tactile_switch_smd]
  S72 = SWITCH-MOMENTARY-2 [package=tactile_switch_smd]
  S73 = SWITCH-MOMENTARY-2 [package=tactile_switch_smd]
  S74 = SWITCH-MOMENTARY-2 [package=tactile_switch_smd]
  S75 = SWITCH-MOMENTARY-2 [package=tactile_switch_smd]
  S76 = SWITCH-MOMENTARY-2 [package=tactile_switch_smd]
  S77 = SWITCH-MOMENTARY-2 [package=tactile_switch_smd]
  S78 = SWITCH-MOMENTARY-2 [package=tactile_switch_smd]
  S79 = SWITCH-MOMENTARY-2 [package=tactile_switch_smd]
  S80 = SWITCH-MOMENTARY-2 [package=tactile_switch_smd]
  S81 = SWITCH-MOMENTARY-2 [package=tactile_switch_smd]
  S82 = SWITCH-MOMENTARY-2 [package=tactile_switch_smd]
  S83 = SWITCH-MOMENTARY-2 [package=tactile_switch_smd]
  S84 = SWITCH-MOMENTARY-2 [package=tactile_switch_smd]
  S85 = SWITCH-MOMENTARY-2 [package=tactile_switch_smd]
  S86 = SWITCH-MOMENTARY-2 [package=tactile_switch_smd]
  S87 = SWITCH-MOMENTARY-2 [package=tactile_switch_smd]
  S88 = SWITCH-MOMENTARY-2 [package=tactile_switch_smd]
  R65 = Resistor [tolerance=±5% resistance=22k package=THT]
  R66 = Resistor [tolerance=±5% resistance=22k package=THT]
  R67 = Resistor [tolerance=±5% resistance=10k package=THT]
  R68 = Resistor [tolerance=±5% resistance=22k package=THT]
  R69 = Resistor [tolerance=±5% resistance=22k package=THT]
  R70 = Resistor [tolerance=±5% resistance=10k package=THT]
  R71 = Resistor [tolerance=±5% resistance=10k package=THT]
  R72 = Resistor [tolerance=±5% resistance=22k package=THT]
  R73 = Resistor [tolerance=±5% resistance=22k package=THT]
  R74 = Resistor [tolerance=±5% resistance=10k package=THT]
  R75 = Resistor [tolerance=±5% resistance=22k package=THT]
  R76 = Resistor [tolerance=±5% resistance=22k package=THT]
  R77 = Resistor [tolerance=±5% resistance=22k package=THT]
  R78 = Resistor [tolerance=±5% resistance=22k package=THT]
  R79 = Resistor [tolerance=±5% resistance=10k package=THT]
  R80 = Resistor [tolerance=±5% resistance=22k package=THT]
  R81 = Resistor [tolerance=±5% resistance=10k package=THT]
  R82 = Resistor [tolerance=±5% resistance=22k package=THT]
  R83 = Resistor [tolerance=±5% resistance=22k package=THT]
  R84 = Resistor [tolerance=±5% resistance=10k package=THT]
  R85 = Resistor [tolerance=±5% resistance=10k package=THT]
  R86 = Resistor [tolerance=±5% resistance=22k package=THT]
  R87 = Resistor [tolerance=±5% resistance=10k package=THT]
  R88 = Resistor [tolerance=±5% resistance=10k package=THT]
  R89 = Resistor [tolerance=±5% resistance=22k package=THT]
  R90 = Resistor [tolerance=±5% resistance=10k package=THT]
  R91 = Resistor [tolerance=±5% resistance=10k package=THT]
  R92 = Resistor [tolerance=±5% resistance=10k package=THT]
  R93 = Resistor [tolerance=±5% resistance=22k package=THT]
  R94 = Resistor [tolerance=±5% resistance=10k package=THT]
  R95 = Resistor [tolerance=±5% resistance=22k package=THT]
  R96 = Resistor [tolerance=±5% resistance=10k package=THT]
  R97 = Resistor [tolerance=±5% resistance=22k package=THT]
  R98 = Resistor [tolerance=±5% resistance=10k package=THT]
  R99 = Resistor [tolerance=±5% resistance=22k package=THT]
  R100 = Resistor [tolerance=±5% resistance=10k package=THT]
  R101 = Resistor [tolerance=±5% resistance=10k package=THT]
  R102 = Resistor [tolerance=±5% resistance=22k package=THT]
  R103 = Resistor [tolerance=±5% resistance=22k package=THT]
  R104 = Resistor [tolerance=±5% resistance=22k package=THT]
  R105 = Resistor [tolerance=±5% resistance=10k package=THT]
  R106 = Resistor [tolerance=±5% resistance=22k package=THT]
  R107 = Resistor [tolerance=±5% resistance=22k package=THT]
  R108 = Resistor [tolerance=±5% resistance=22k package=THT]
  R109 = Resistor [tolerance=±5% resistance=22k package=THT]
  R110 = Resistor [tolerance=±5% resistance=22k package=THT]
  R111 = Resistor [tolerance=±5% resistance=22k package=THT]
  R112 = Resistor [tolerance=±5% resistance=10k package=THT]
  R113 = Resistor [tolerance=±5% resistance=10k package=THT]
  R114 = Resistor [tolerance=±5% resistance=10k package=THT]
  R115 = Resistor [tolerance=±5% resistance=22k package=THT]
  R116 = Resistor [tolerance=±5% resistance=10k package=THT]
  R117 = Resistor [tolerance=±5% resistance=10k package=THT]
  R118 = Resistor [tolerance=±5% resistance=22k package=THT]
  R119 = Resistor [tolerance=±5% resistance=10k package=THT]
  R120 = Resistor [tolerance=±5% resistance=22k package=THT]
  R121 = Resistor [tolerance=±5% resistance=10k package=THT]
  R122 = Resistor [tolerance=±5% resistance=22k package=THT]
  R123 = Resistor [tolerance=±5% resistance=22k package=THT]
  R124 = Resistor [tolerance=±5% resistance=22k package=THT]
  R125 = Resistor [tolerance=±5% resistance=10k package=THT]
  R126 = Resistor [tolerance=±5% resistance=22k package=THT]
  R127 = Resistor [tolerance=±5% resistance=22k package=THT]
  R128 = Resistor [tolerance=±5% resistance=10k package=THT]
  R2_9 = Resistor [tolerance=±5% resistance=22k package=THT]

nets:
  N1: MUX01.pin1, R65.Pin_1, R92.Pin_1
  N2: MUX01.pin2, R85.Pin_1, R97.Pin_1
  N3: MUX01.pin3, Part1.A0
  N4: MUX01.pin4, R121.Pin_1, R123.Pin_1
  N5: MUX01.pin5, R66.Pin_1, R91.Pin_1
  N6: MUX01.pin6, MUX01.pin7, MUX01.pin8, Part1.GND, R136.Pin_0, R2_5.Pin_0, R38.Pin_0, R57.Pin_0, R89.Pin_0, R99.Pin_0, R118.Pin_0, R122.Pin_0
  N7: MUX01.pin9, Part1.D4
  N8: MUX01.pin10, Part1.D3_PWM
  N9: MUX01.pin11, Part1.D2
  N10: MUX01.pin12, R56.Pin_1, R64.Pin_1
  N11: MUX01.pin13, R129.Pin_1, R143.Pin_1
  N12: MUX01.pin14, R144.Pin_1, R2_9.Pin_1
  N13: MUX01.pin15, R47.Pin_1, R48.Pin_1
  N14: MUX01.pin16, Part1.5V, S25.1, S26.1, S27.1, S28.1, S29.1, S30.1, S31.1, S32.1, S33.1, S34.1, S35.1, S36.1, S37.1, S38.1, S39.1, S40.1, S41.1, S42.1, S43.1, S44.1, S45.1, S46.1, S47.1, S48.1, S49.1, S50.1, S51.1, S52.1, S53.1, S54.1, S55.1, S56.1, S57.1, S58.1, S59.1, S60.1, S61.1, S62.1, S63.1, S64.1, S65.1, S66.1, S67.1, S68.1, S69.1, S70.1, S71.1, S72.1, S73.1, S74.1, S75.1, S76.1, S77.1, S78.1, S79.1, S80.1, S81.1, S82.1, S83.1, S84.1, S85.1, S86.1, S87.1, S88.1
  N15: S25.2, R134.Pin_0
  N16: S26.2, R7.Pin_0
  N17: S27.2, R133.Pin_0
  N18: S28.2, R135.Pin_0
  N19: S29.2, R130.Pin_0
  N20: S30.2, R131.Pin_0
  N21: S31.2, R129.Pin_0
  N22: S32.2, R132.Pin_0
  N23: R130.Pin_1, R142.Pin_1, R143.Pin_0
  N24: R131.Pin_1, R141.Pin_1, R142.Pin_0
  N25: R132.Pin_1, R140.Pin_1, R141.Pin_0
  N26: R133.Pin_1, R139.Pin_1, R140.Pin_0
  N27: R134.Pin_1, R138.Pin_1, R139.Pin_0
  N28: R7.Pin_1, R137.Pin_1, R138.Pin_0
  N29: R135.Pin_1, R136.Pin_1, R137.Pin_0
  N30: S33.2, R2_8.Pin_0
  N31: S34.2, R2_9.Pin_0
  N32: S35.2, R2.Pin_0
  N33: S36.2, R2_6.Pin_0
  N34: S37.2, R2_4.Pin_0
  N35: S38.2, R2_2.Pin_0
  N36: S39.2, R2_3.Pin_0
  N37: S40.2, R2_7.Pin_0
  N38: R2.Pin_1, R147.Pin_1, R148.Pin_0
  N39: R2_2.Pin_1, R145.Pin_1, R146.Pin_0
  N40: R2_3.Pin_1, R25.Pin_1, R149.Pin_0
  N41: R2_4.Pin_1, R2_5.Pin_1, R25.Pin_0
  N42: R144.Pin_0, R2_6.Pin_1, R148.Pin_1
  N43: R145.Pin_0, R2_7.Pin_1, R149.Pin_1
  N44: R146.Pin_1, R147.Pin_0, R2_8.Pin_1
  N45: S41.2, R39.Pin_0
  N46: S42.2, R47.Pin_0
  N47: S43.2, R40.Pin_0
  N48: S44.2, R34.Pin_0
  N49: S45.2, R42.Pin_0
  N50: S46.2, R36.Pin_0
  N51: S47.2, R33.Pin_0
  N52: S48.2, R37.Pin_0
  N53: R33.Pin_1, R35.Pin_1, R44.Pin_0
  N54: R34.Pin_1, R41.Pin_1, R48.Pin_0
  N55: R35.Pin_0, R38.Pin_1, R42.Pin_1
  N56: R36.Pin_1, R45.Pin_0, R46.Pin_1
  N57: R37.Pin_1, R44.Pin_1, R46.Pin_0
  N58: R39.Pin_1, R43.Pin_0, R45.Pin_1
  N59: R40.Pin_1, R41.Pin_0, R43.Pin_1
  N60: S49.2, R53.Pin_0
  N61: S50.2, R64.Pin_0
  N62: S51.2, R52.Pin_0
  N63: S52.2, R51.Pin_0
  N64: S53.2, R49.Pin_0
  N65: S54.2, R63.Pin_0
  N66: S55.2, R62.Pin_0
  N67: S56.2, R61.Pin_0
  N68: R49.Pin_1, R57.Pin_1, R60.Pin_0
  N69: R50.Pin_0, R52.Pin_1, R58.Pin_1
  N70: R50.Pin_1, R51.Pin_1, R56.Pin_0
  N71: R53.Pin_1, R55.Pin_1, R58.Pin_0
  N72: R54.Pin_0, R59.Pin_1, R61.Pin_1
  N73: R54.Pin_1, R55.Pin_0, R63.Pin_1
  N74: R59.Pin_0, R60.Pin_1, R62.Pin_1
  N75: S57.2, R109.Pin_0
  N76: S58.2, R120.Pin_0
  N77: S59.2, R75.Pin_0
  N78: S60.2, R93.Pin_0
  N79: S61.2, R65.Pin_0
  N80: S62.2, R97.Pin_0
  N81: S63.2, R123.Pin_0
  N82: S64.2, R66.Pin_0
  N83: S65.2, R82.Pin_0
  N84: S66.2, R124.Pin_0
  N85: S67.2, R108.Pin_0
  N86: S68.2, R126.Pin_0
  N87: S69.2, R77.Pin_0
  N88: S70.2, R80.Pin_0
  N89: S71.2, R83.Pin_0
  N90: S72.2, R103.Pin_0
  N91: S73.2, R111.Pin_0
  N92: S74.2, R104.Pin_0
  N93: S75.2, R107.Pin_0
  N94: S76.2, R127.Pin_0
  N95: S77.2, R110.Pin_0
  N96: S78.2, R115.Pin_0
  N97: S79.2, R76.Pin_0
  N98: S80.2, R86.Pin_0
  N99: S81.2, R69.Pin_0
  N100: S82.2, R73.Pin_0
  N101: S83.2, R68.Pin_0
  N102: S84.2, R72.Pin_0
  N103: S85.2, R95.Pin_0
  N104: S86.2, R102.Pin_0
  N105: S87.2, R78.Pin_0
  N106: S88.2, R106.Pin_0
  N107: R67.Pin_0, R94.Pin_1, R109.Pin_1
  N108: R67.Pin_1, R82.Pin_1, R100.Pin_0
  N109: R68.Pin_1, R90.Pin_1, R114.Pin_0
  N110: R69.Pin_1, R79.Pin_1, R125.Pin_0
  N111: R70.Pin_0, R86.Pin_1, R87.Pin_1
  N112: R70.Pin_1, R93.Pin_1, R113.Pin_0
  N113: R71.Pin_0, R113.Pin_1, R126.Pin_1
  N114: R71.Pin_1, R80.Pin_1, R121.Pin_0
  N115: R72.Pin_1, R88.Pin_0, R119.Pin_1
  N116: R73.Pin_1, R101.Pin_1, R112.Pin_0
  N117: R74.Pin_0, R102.Pin_1, R112.Pin_1
  N118: R74.Pin_1, R81.Pin_0, R115.Pin_1
  N119: R75.Pin_1, R98.Pin_0, R105.Pin_1
  N120: R76.Pin_1, R105.Pin_0, R116.Pin_1
  N121: R77.Pin_1, R92.Pin_0, R100.Pin_1
  N122: R78.Pin_1, R114.Pin_1, R116.Pin_0
  N123: R79.Pin_0, R111.Pin_1, R118.Pin_1
  N124: R81.Pin_1, R84.Pin_0, R120.Pin_1
  N125: R83.Pin_1, R91.Pin_0, R96.Pin_1
  N126: R84.Pin_1, R124.Pin_1, R128.Pin_0
  N127: R85.Pin_0, R103.Pin_1, R128.Pin_1
  N128: R87.Pin_0, R88.Pin_1, R106.Pin_1
  N129: R89.Pin_1, R90.Pin_0, R127.Pin_1
  N130: R94.Pin_0, R110.Pin_1, R117.Pin_1
  N131: R95.Pin_1, R117.Pin_0, R125.Pin_1
  N132: R96.Pin_0, R98.Pin_1, R108.Pin_1
  N133: R99.Pin_1, R104.Pin_1, R119.Pin_0
  N134: R101.Pin_0, R107.Pin_1, R122.Pin_1

// code stored in the sketch: Untitled2.ino
void setup() {

}

void loop() {
	Serial.println(analogRead(A0));
}
